# Fritzing sketch LED_sensor (saved by Fritzing 0.8.5b)
circuit board: 16.9333cm x 5.64444cm
breadboards: 1

parts:
  LED1 = LED - 5mm [color="White (6500K)" package="5 mm [THT]"]
  R1 = Resistor [tolerance=±5% resistance=330 package=THT]
  R2 = Photocell (LDR) [package=THT]
  R3 = Resistor [tolerance=±5% resistance=330 package=THT]
  Part1 = Arduino Uno (Rev3)

nets:
  N1: LED1.cathode, Part1.D11_PWM/MOSI
  N2: LED1.anode, R1.Pin_0
  N3: R1.Pin_1, R2.pin_0, Part1.5V
  N4: R2.pin_1, R3.Pin_0, Part1.A0
  N5: R3.Pin_1, Part1.GND
