# Fritzing sketch LED_sensor (saved by Fritzing 0.8.5b)
circuit board: 16.9333cm x 5.64444cm
breadboards: 1

parts:
  R2 = Photocell (LDR) [package=THT]
  R3 = Resistor [tolerance=±5% resistance=330 package=THT]
  Part1 = Arduino Uno (Rev3)
  R1 = Resistor [tolerance=±5% resistance=330 package=THT]
  LED1 = LED - 5mm [color="White (6500K)" package="5 mm [THT]"]

nets (from the breadboard view):
  N1: R2.pin_0, Part1.5V
  N2: R2.pin_1, R3.Pin_1, Part1.A0
  N3: R3.Pin_0, Part1.GND, R1.Pin_1
  N4: Part1.A1, Part1.D11_PWM/MOSI, LED1.cathode
  N5: R1.Pin_0, LED1.anode
